# Fritzing sketch receiver_normal_wiring (saved by Fritzing 0.9.10b)

parts:
  U1 = ESP32-38PinWide [part_number=ESP32-38PinWide]
  元件1 = Motor Driver 1A Dual TB6612FNG
  M1 = DC Motor [voltage_(max)=6V voltage_(min)=3V]
  M2 = DC Motor [voltage_(max)=6V voltage_(min)=3V]

nets:
  N1: U1.3.3, 元件1.VCC
  N2: U1.GPIO25, 元件1.PWMB
  N3: U1.GPIO26, 元件1.BIN1
  N4: U1.GPIO27, 元件1.BIN2
  N5: U1.VIN, 元件1.VM
  N6: U1.GPIO15, 元件1.PWMA
  N7: U1.GPIO16, 元件1.AIN1
  N8: U1.GPIO17, 元件1.AIN2
  N9: U1.GPIO18, 元件1.STBY
  GND: U1.GND, 元件1.GND
  N10: 元件1.B01, M1.pin_2
  N11: 元件1.B02, M1.pin_1
  N12: 元件1.A02, M2.pin_1
  N13: 元件1.A01, M2.pin_2

custom parts:
  ESP32-38PinWide: Generic 38-Pin ESP32 with wide format (only access to one side of pins on a breadboard) based on Stephen Lilley's HiLetgo ESP-WROOM-32 ESP32 ESP-32S Development Board.
