# Fritzing sketch transmitter_accelerometer_wiring (saved by Fritzing 0.9.10b)
breadboards: 1

parts:
  U1 = ESP32-38PinWide [part_number=ESP32-38PinWide]
  元件1 = Triple Axis Accelerometer Breakout - ADXL335

nets:
  N1: U1.3.3, 元件1.VCC
  N2: U1.GPIO36, 元件1.ZOUT
  N3: U1.GPIO34, 元件1.YOUT
  N4: U1.GPIO35, 元件1.XOUT
  N5: U1.GPIO11, 元件1.GND

custom parts:
  ESP32-38PinWide: Generic 38-Pin ESP32 with wide format (only access to one side of pins on a breadboard) based on Stephen Lilley's HiLetgo ESP-WROOM-32 ESP32 ESP-32S Development Board.
