# Fritzing sketch transmitter_joystick_wiring (saved by Fritzing 0.9.10b)

parts:
  U1 = ESP32-38PinWide [part_number=ESP32-38PinWide]
  元件1 = Thumb Joystick

nets:
  N1: U1.3.3, 元件1.VCC
  N2: U1.GPIO35, 元件1.SEL
  N3: U1.GPIO32, 元件1.HORZ
  N4: U1.GPIO33, 元件1.VERT
  GND: U1.GND, 元件1.GND

custom parts:
  ESP32-38PinWide: Generic 38-Pin ESP32 with wide format (only access to one side of pins on a breadboard) based on Stephen Lilley's HiLetgo ESP-WROOM-32 ESP32 ESP-32S Development Board.
